# Fritzing sketch Anvil (saved by Fritzing 0.9.3b)
breadboards: 1

parts:
  Piezo1 = Piezo Speaker - PC Mount [part_number=COM-07950]
  LED1 = LED - 5mm [color="Blue (430nm)" package="5 mm [THT]"]
  LED2 = LED - 5mm [color="Red (633nm)" package="5 mm [THT]"]
  R1 = Resistor [tolerance=±5% resistance=330 package=THT]
  R2 = Resistor [tolerance=±5% resistance=330 package=THT]
  Raspberry_Pi_1 = Raspberry Pi 3 [part_number=RPI-3-V1.2]

nets:
  GND: Piezo1.GND, R1.Pin_1, R2.Pin_1, Raspberry_Pi_1.GND
  N1: Piezo1.VCC, Raspberry_Pi_1.GIPO22
  N2: LED1.cathode, R2.Pin_0
  N3: LED1.anode, Raspberry_Pi_1.GIPO27
  N4: LED2.cathode, R1.Pin_0
  N5: LED2.anode, Raspberry_Pi_1.GIPO17

custom parts:
  Piezo Speaker - PC Mount: This is a small 12mm round speaker that operates around the audible 2kHz range. You can use these speakers to create simple music or user interfaces. Each speaker is PTH solderable and requires an operating voltage of 3.5-5V with a mean current of 35mA max. These speakers also have a typical sound output of 95 dBA and a coil resistance of 42 ±6.3 ohms.
